# Fritzing sketch lerBotao_v2 (saved by Fritzing 0.9.3b)
breadboards: 1

parts:
  Part1 = Arduino Nano (Rev3.0) (ICSP)
  S1 = Pushbutton [package="[THT]"]

nets:
  N1: Part1.D5, S1.Pin_1, S1.Pin_2
  N2: Part1.3V3, S1.Pin_3, S1.Pin_4
