# Fritzing sketch sensorBrilhoLed (saved by Fritzing 0.9.3b)
breadboards: 1

parts:
  Part1 = Arduino Nano (Rev3.0) (ICSP)
  U1 = POT [package=pot_mammoth]
  LED1 = smd LED [color="Red (633nm)" package="0805 [SMD]"]

nets:
  N1: Part1.GND, U1.S, LED1.cathode
  N2: Part1.D3, LED1.anode
  N3: Part1.A0, U1.A
  N4: Part1.3V3, U1.E
